# Fritzing sketch ARDUINO POWER SCHEMATIC (saved by Fritzing 0.9.3b)
breadboards: 1

parts:
  D3 = Rectifier Diode [part_number=1N4001 package="Melf DO-213 AB [SMD]"]
  TIP120 = NPN-Transistor [package="TO92 [THT]"]
  R1 = Resistor [tolerance=±5% resistance=220 package=THT]
  R2 = Resistor [tolerance=±5% resistance=1k package=THT]
  R3 = Resistor [tolerance=±5% resistance=1k package=THT]
  R4 = Resistor [tolerance=±5% resistance=1k package=THT]
  R5 = Resistor [tolerance=±5% resistance=1k package=THT]
  D4 = Rectifier Diode [part_number=1N4001 package="Melf DO-213 AB [SMD]"]
  LED2 = smd LED [color="Red (633nm)" package="1206 [SMD]"]
  FLASHING_LED = smd LED [color="Red (633nm)" package="1206 [SMD]"]
  Power_plug1 = Power plug
  VCC1 = Battery block 9V

nets (from the schematic view):
  ARDUINO VIN: D3.cathode, R4.Pin_1, D4.cathode
  N1: D3.anode, R5.Pin_0, Power_plug1.VCC
  GND: TIP120.E, R1.Pin_0, R2.Pin_0, FLASHING_LED.cathode, Power_plug1.GND, VCC1.-
  N2: TIP120.B, R5.Pin_1
  N3: TIP120.C, R4.Pin_0, FLASHING_LED.anode
  N4: R1.Pin_1, LED2.cathode
  A0: R2.Pin_1, R3.Pin_1
  N5: R3.Pin_0, D4.anode, VCC1.+
  D2: LED2.anode

notes:
  REDUNDANT POWER CIRCUIT, REDUNDANT ARDUINO POWER CIRCUIT WITH FLASHING POWER CUT LED & LOW BATTERY LED, 1.0
  CONOR WALSH 2016
  D2
  A0
  VIN
  GND
